// Logisim project 1.circ as structural Verilog: 1 circuit, main circuit main
module main (
  input  A,
  input  B,
  input  C,
  input  D,
  output f,
  output g
);

  wire A_t, ABC_out, B_nD_nC_out, B_nD_out, B_t, BC_out, C_t, clock, D_t, go, nAB_out, nABC_out, nABD_out,
       not_1_out, not_2_out, not_3_out, not_4_out, Reset_out, t_ff_1_q, t_ff_2_q, t_ff_3_q, t_ff_4_q;

  not not_1 (not_1_out, A_t);
  not not_2 (not_2_out, B_t);
  not not_3 (not_3_out, C_t);
  not not_4 (not_4_out, D_t);
  // Probe on {A_t, B_t, C_t, D_t}
  Clock clock_1 (.out(clock));
  // Probe on {A_t, B_t, C_t, D_t}
  // Probe on f
  T_Flip_Flop t_ff_1 (.clk(clock), .T(1'b1), .Q(t_ff_1_q), .Qn(D_t), .preset(Reset_out), .en(go));  // open: reset
  // Probe on g
  T_Flip_Flop t_ff_2 (.clk(t_ff_1_q), .T(1'b1), .Q(t_ff_2_q), .Qn(C_t), .preset(Reset_out));  // open: reset, en
  and nABD (nABD_out, not_1_out, B_t, D_t);
  TTY #(.rows(1), .cols(18)) tty_1 (.data({6'b011000, f}), .clk(clock), .we(go), .clr(Reset_out));
  T_Flip_Flop t_ff_3 (.clk(t_ff_4_q), .T(1'b1), .Q(t_ff_3_q), .Qn(A_t), .preset(Reset_out));  // open: reset, en
  T_Flip_Flop t_ff_4 (.clk(t_ff_2_q), .T(1'b1), .Q(t_ff_4_q), .Qn(B_t), .preset(Reset_out));  // open: reset, en
  TTY #(.rows(1), .cols(18)) tty_2 (.data({6'b011000, g}), .clk(clock), .we(go), .clr(Reset_out));
  and nABC (nABC_out, not_1_out, C_t, B_t);
  T_Flip_Flop t_ff_5 (.clk(t_ff_3_q), .T(1'b1), .Q(go), .preset(Reset_out));  // open: Qn, reset, en
  Button Reset (.out(Reset_out));
  and ABC (ABC_out, A_t, B_t, C_t);
  and B_nD_nC (B_nD_nC_out, B_t, not_4_out, not_3_out);
  or or_1 (f, nABD_out, ABC_out, nABC_out, B_nD_nC_out);
  and B_nD (B_nD_out, B_t, not_4_out);
  and nAB (nAB_out, B_t, not_1_out);
  and BC (BC_out, B_t, C_t);
  or or_2 (g, BC_out, B_nD_out, nAB_out);

  // Notes on the sheet:
  //   0000111100001011
  //   0000111100001011
endmodule
