// Logisim project 2.circ as structural Verilog: 2 circuits, main circuit main
module main (
  input  A,
  input  B,
  input  C,
  input  D,
  output f
);

  wire A_t, and_1_out, and_2_out, and_3_out, and_4_out, B_t, C_t, clock_1_out, D_t, go, not_1_out, not_2_out,
       Reset_out, t_ff_1_q, t_ff_2_q, t_ff_3_q, t_ff_4_q;

  not not_1 (not_1_out, C_t);
  not not_2 (not_2_out, D_t);
  // Probe on {A_t, B_t, C_t, D_t}
  T_Flip_Flop t_ff_1 (.clk(clock_1_out), .T(1'b1), .Q(t_ff_1_q), .Qn(D_t), .preset(Reset_out), .en(go));  // open: reset
  Clock clock_1 (.out(clock_1_out));
  and and_1 (and_1_out, B_t, not_1_out, not_2_out);
  and and_2 (and_2_out, A_t, not_1_out, not_2_out);
  // Probe on f
  T_Flip_Flop t_ff_2 (.clk(t_ff_1_q), .T(1'b1), .Q(t_ff_2_q), .Qn(C_t), .preset(Reset_out));  // open: reset, en
  and and_3 (and_3_out, B_t, C_t, D_t);
  TTY #(.rows(1), .cols(18)) tty_1 (.data({6'b011000, f}), .clk(clock_1_out), .we(go), .clr(Reset_out));
  T_Flip_Flop t_ff_3 (.clk(t_ff_2_q), .T(1'b1), .Q(t_ff_3_q), .Qn(B_t), .preset(Reset_out));  // open: reset, en
  and and_4 (and_4_out, A_t, C_t, D_t);
  T_Flip_Flop t_ff_4 (.clk(t_ff_3_q), .T(1'b1), .Q(t_ff_4_q), .Qn(A_t), .preset(Reset_out));  // open: reset, en
  Button Reset (.out(Reset_out));
  T_Flip_Flop t_ff_5 (.clk(t_ff_4_q), .T(1'b1), .Q(go), .preset(Reset_out));  // open: Qn, reset, en
  or or_1 (f, and_1_out, and_2_out, and_3_out, and_4_out);

  // Notes on the sheet:
  //   000010011001d00d
endmodule

module Tester (
);

  wire A, B, C, clock_1_out, D, f, go, Reset_out, t_ff_1_q, t_ff_2_q, t_ff_3_q, t_ff_4_q;

  Clock clock_1 (.out(clock_1_out));
  // Probe on f
  // Probe on {A, B, C, D}
  T_Flip_Flop t_ff_1 (.clk(clock_1_out), .T(1'b1), .Q(t_ff_1_q), .Qn(D), .preset(Reset_out), .en(go));  // open: reset
  T_Flip_Flop t_ff_2 (.clk(t_ff_1_q), .T(1'b1), .Q(t_ff_2_q), .Qn(C), .preset(Reset_out));  // open: reset, en
  TTY #(.rows(1), .cols(18)) tty_1 (.data({6'b011000, f}), .clk(clock_1_out), .we(go), .clr(Reset_out));
  T_Flip_Flop t_ff_3 (.clk(t_ff_2_q), .T(1'b1), .Q(t_ff_3_q), .Qn(B), .preset(Reset_out));  // open: reset, en
  T_Flip_Flop t_ff_4 (.clk(t_ff_3_q), .T(1'b1), .Q(t_ff_4_q), .Qn(A), .preset(Reset_out));  // open: reset, en
  Button Reset (.out(Reset_out));
  T_Flip_Flop t_ff_5 (.clk(t_ff_4_q), .T(1'b1), .Q(go), .preset(Reset_out));  // open: Qn, reset, en

  // Notes on the sheet:
  //   000010011001d00d
endmodule
