// Logisim project 3.circ as structural Verilog: 1 circuit, main circuit main
module main (
  input  A,
  input  B,
  input  C,
  input  D,
  input  E,
  input  F,
  output out_7,
  output out_8,
  output out_9
);

  wire A_t, adder_1_cout, adder_1_out, adder_2_cout, adder_2_out, adder_3_cout, adder_3_out, adder_4_cout,
       and_1_out, B_t, C_t, clock_1_out, D_t, E_t, F_t, go, Reset_out, t_ff_1_q, t_ff_2_q, t_ff_3_q,
       t_ff_4_q, t_ff_5_q, t_ff_6_q;

  // Probe on {A_t, B_t, C_t, D_t, E_t, F_t}
  Adder #(.width(1)) adder_1 (.a(B_t), .b(C_t), .out(adder_1_out), .cin(A_t), .cout(adder_1_cout));
  Adder #(.width(1)) adder_2 (.a(E_t), .b(F_t), .out(adder_2_out), .cin(D_t), .cout(adder_2_cout));
  // Probe on {out_7, out_8, out_9}
  TTY #(.rows(1), .cols(65)) tty_1 (.data({4'b0110, out_7, out_8, out_9}), .clk(clock_1_out), .we(go), .clr(Reset_out));
  T_Flip_Flop t_ff_1 (.clk(clock_1_out), .T(1'b1), .Q(t_ff_1_q), .Qn(F_t), .preset(Reset_out), .en(go));  // open: reset
  Clock clock_1 (.out(clock_1_out));
  Adder #(.width(1)) adder_3 (.a(adder_1_cout), .b(adder_2_cout), .out(adder_3_out), .cout(adder_3_cout));  // open: cin
  Adder #(.width(1)) adder_4 (.a(adder_1_out), .b(adder_2_out), .out(out_9), .cout(adder_4_cout));  // open: cin
  T_Flip_Flop t_ff_2 (.clk(t_ff_1_q), .T(1'b1), .Q(t_ff_2_q), .Qn(E_t), .preset(Reset_out));  // open: reset, en
  T_Flip_Flop t_ff_3 (.clk(t_ff_2_q), .T(1'b1), .Q(t_ff_3_q), .Qn(D_t), .preset(Reset_out));  // open: reset, en
  or or_1 (out_7, adder_3_cout, and_1_out);
  and and_1 (and_1_out, adder_3_out, adder_4_cout);
  T_Flip_Flop t_ff_4 (.clk(t_ff_3_q), .T(1'b1), .Q(t_ff_4_q), .Qn(C_t), .preset(Reset_out));  // open: reset, en
  xor xor_1 (out_8, adder_3_out, adder_4_cout);
  T_Flip_Flop t_ff_5 (.clk(t_ff_4_q), .T(1'b1), .Q(t_ff_5_q), .Qn(B_t), .preset(Reset_out));  // open: reset, en
  T_Flip_Flop t_ff_6 (.clk(t_ff_5_q), .T(1'b1), .Q(t_ff_6_q), .Qn(A_t), .preset(Reset_out));  // open: reset, en
  Button Reset (.out(Reset_out));
  T_Flip_Flop t_ff_7 (.clk(t_ff_6_q), .T(1'b1), .Q(go), .preset(Reset_out));  // open: Qn, reset, en

  // Other names for the same wires on the sheet: X0 = out_9; X1 = out_8; X2 = out_7

  // Notes on the sheet:
  //   0112122312232334122323342334344512232334233434452334344534454556
endmodule
