// Logisim project 4.circ as structural Verilog: 1 circuit, main circuit main
module main (
  input  in_1,
  input  in_2,
  input  in_3,
  output out_4
);

  wire A, and_1_out, and_2_out, and_3_out, and_4_out, and_5_out, and_6_out, and_7_out, and_8_out, B, C,
       clock_1_out, go, not_1_out, not_2_out, not_3_out, Reset_out, t_ff_1_q, t_ff_2_q, t_ff_3_q;

  Clock clock_1 (.out(clock_1_out));
  not not_1 (not_1_out, A);
  not not_2 (not_2_out, B);
  not not_3 (not_3_out, C);
  // Probe on out_4
  // Probe on {A, B, C}
  T_Flip_Flop t_ff_1 (.clk(clock_1_out), .T(1'b1), .Q(t_ff_1_q), .Qn(C), .preset(Reset_out), .en(go));  // open: reset
  T_Flip_Flop t_ff_2 (.clk(t_ff_1_q), .T(1'b1), .Q(t_ff_2_q), .Qn(B), .preset(Reset_out));  // open: reset, en
  TTY #(.rows(1), .cols(10)) tty_1 (.data({6'b011000, out_4}), .clk(clock_1_out), .we(go), .clr(Reset_out));
  T_Flip_Flop t_ff_3 (.clk(t_ff_2_q), .T(1'b1), .Q(t_ff_3_q), .Qn(A), .preset(Reset_out));  // open: reset, en
  and and_1 (and_1_out, A, C, B);
  and and_2 (and_2_out, not_1_out, C, B);
  and and_3 (and_3_out, A, C, not_2_out);
  and and_4 (and_4_out, not_1_out, C, not_2_out);
  and and_5 (and_5_out, A, not_3_out, B);
  and and_6 (and_6_out, not_1_out, not_3_out, B);
  and and_7 (and_7_out, A, not_2_out);
  and and_8 (and_8_out, not_1_out, not_3_out, not_2_out);
  Button Reset (.out(Reset_out));
  T_Flip_Flop t_ff_4 (.clk(t_ff_3_q), .T(1'b1), .Q(go), .preset(Reset_out));  // open: Qn, reset, en
  or or_1 (out_4, and_2_out, and_3_out, and_4_out, and_5_out, and_6_out);

  // Other names for the same wires on the sheet: f = out_4

  // Notes on the sheet:
  //   01110110
endmodule
