// Logisim project 5.circ as structural Verilog: 1 circuit, main circuit main
module main (
  input  A,
  input  B,
  input  C,
  output out_4
);

  wire A_t, and_1_out, B_t, C_t, clock_1_out, go, not_1_out, or_1_out, Reset_out, t_ff_1_q, t_ff_2_q,
       t_ff_3_q;

  not not_1 (not_1_out, A_t);
  and and_1 (and_1_out, B_t, not_1_out);
  or or_1 (or_1_out, B_t, not_1_out);
  Multiplexer multiplexer_1 (.in0(or_1_out), .in1(and_1_out), .out(out_4), .sel(C_t));  // open: en
  Clock clock_1 (.out(clock_1_out));
  // Probe on {A_t, B_t, C_t}
  T_Flip_Flop t_ff_1 (.clk(clock_1_out), .T(1'b1), .Q(t_ff_1_q), .Qn(C_t), .preset(Reset_out), .en(go));  // open: reset
  // Probe on out_4
  T_Flip_Flop t_ff_2 (.clk(t_ff_1_q), .T(1'b1), .Q(t_ff_2_q), .Qn(B_t), .preset(Reset_out));  // open: reset, en
  TTY #(.rows(1), .cols(10)) tty_1 (.data({6'b011000, out_4}), .clk(clock_1_out), .we(go), .clr(Reset_out));
  T_Flip_Flop t_ff_3 (.clk(t_ff_2_q), .T(1'b1), .Q(t_ff_3_q), .Qn(A_t), .preset(Reset_out));  // open: reset, en
  Button Reset (.out(Reset_out));
  T_Flip_Flop t_ff_4 (.clk(t_ff_3_q), .T(1'b1), .Q(go), .preset(Reset_out));  // open: Qn, reset, en

  // Other names for the same wires on the sheet: f = out_4

  // Notes on the sheet:
  //   10110010
endmodule
