// Logisim project 6.circ as structural Verilog: 1 circuit, main circuit main
module main (
  input  w1,
  input  w2,
  input  w3,
  output a,
  output b,
  output c
);

  wire clock_1_out, go, not_1_out, not_2_out, not_3_out, not_4_out, not_5_out, not_6_out, nw0_nW1_out,
       nw0_nw2_out, nW1_nW2_out, nw3_nw2_out, Reset_out, t_ff_1_q, t_ff_2_q, t_ff_3_q, w0, w0w2_out, w1_t,
       W1W0_out, w2_nw3_out, w2_t, w3_nw2_out, w3_t;

  not not_1 (not_1_out, w0);
  not not_2 (not_2_out, w2_t);
  not not_3 (not_3_out, w3_t);
  not not_4 (not_4_out, w1_t);
  and w3_nw2 (w3_nw2_out, not_2_out, w3_t);
  and w0w2 (w0w2_out, w0, w2_t);
  and nw3_nw2 (nw3_nw2_out, not_2_out, not_3_out);
  and w2_nw3 (w2_nw3_out, w2_t, not_3_out);
  or u_c (c, not_4_out, w2_nw3_out, W1W0_out);
  and nw0_nw2 (nw0_nw2_out, not_1_out, not_2_out);
  or u_a (a, w0w2_out, nw0_nw2_out, w3_nw2_out, w1_t);
  and nw0_nW1 (nw0_nW1_out, not_1_out, not_4_out);
  and nW1_nW2 (nW1_nW2_out, not_4_out, not_2_out);
  and W1W0 (W1W0_out, w1_t, w0);
  or u_b (b, nw0_nW1_out, W1W0_out, nw3_nw2_out, nW1_nW2_out);
  // Probe on {w3_t, w2_t, w1_t, w0}
  Clock clock_1 (.out(clock_1_out));
  T_Flip_Flop t_ff_1 (.clk(clock_1_out), .T(1'b1), .Q(t_ff_1_q), .Qn(w0), .preset(Reset_out), .en(go));  // open: reset
  nand nand_1 (go, not_5_out, w1_t, not_6_out, w3_t);
  // Probe on a
  // Probe on b
  // Probe on c
  T_Flip_Flop t_ff_2 (.clk(t_ff_1_q), .T(1'b1), .Q(t_ff_2_q), .Qn(w1_t), .preset(Reset_out));  // open: reset, en
  TTY #(.rows(1), .cols(18)) tty_1 (.data({6'b011000, a}), .clk(clock_1_out), .we(go), .clr(Reset_out));
  TTY #(.rows(1), .cols(18)) tty_2 (.data({6'b011000, b}), .clk(clock_1_out), .we(go), .clr(Reset_out));
  TTY #(.rows(1), .cols(18)) tty_3 (.data({6'b011000, c}), .clk(clock_1_out), .we(go), .clr(Reset_out));
  T_Flip_Flop t_ff_3 (.clk(t_ff_2_q), .T(1'b1), .Q(t_ff_3_q), .Qn(w2_t), .preset(Reset_out));  // open: reset, en
  not not_5 (not_5_out, w0);
  not not_6 (not_6_out, w2_t);
  T_Flip_Flop t_ff_4 (.clk(t_ff_3_q), .T(1'b1), .Qn(w3_t), .preset(Reset_out));  // open: Q, reset, en
  Button Reset (.out(Reset_out));

  // Notes on the sheet:
  //   1011011111
  //   1111100111
  //   1101111111
  //   go until 10
endmodule
