// Logisim project 7.circ as structural Verilog: 1 circuit, main circuit main
module main (
);

  wire A0, A1, A2, C0, C0_out, C1, C1_out, C2, C2_out, C3, C3_out, clock_1_out, D0, D1, D2, D3, D4, D5, D6,
       D7, decoder_1_out4, decoder_1_out5, decoder_1_out6, decoder_1_out7, decoder_1_out9, decoder_1_out11,
       decoder_1_out14, decoder_1_out15, go, not_1_out, not_2_out, not_3_out, not_4_out, not_5_out,
       not_6_out, not_7_out, not_8_out, P0, P1, P2, Reset_out, t_ff_1_q, t_ff_2_q, t_ff_3_q, t_ff_4_q,
       t_ff_5_q, t_ff_6_q, Z0, Z1, Z2, Z3, Z4, Z5, Z6, Z7;
  wire [0:0] multiplexer_1_out;
  wire [3:0] or_4_out;

  ExactlyOne u_C3 (.out(C3_out), .in1(D7), .in2(D4), .in3(D5), .in4(D6));
  or or_1 (or_4_out[3], C3, C3_out);
  ExactlyOne u_C2 (.out(C2_out), .in1(D7), .in2(D3), .in3(D2), .in4(D1));
  T_Flip_Flop t_ff_1 (.clk(clock_1_out), .T(1'b1), .Q(t_ff_1_q), .Qn(P0), .preset(Reset_out), .en(go));  // open: reset
  Clock clock_1 (.out(clock_1_out));
  or or_2 (or_4_out[2], C2, C2_out);
  ExactlyOne u_C1 (.out(C1_out), .in0(D6), .in1(D5), .in2(D3), .in3(D2), .in4(D0));
  Multiplexer #(.select(3), .disabled(0), .enable("false")) multiplexer_1 (
    .in0(Z7), .in1(Z6), .in2(Z5), .in3(Z4), .in4(Z3), .in5(Z2), .in6(Z1), .in7(Z0),
    .out(multiplexer_1_out[0]), .sel({P2, P1, P0}));
  T_Flip_Flop t_ff_2 (.clk(t_ff_1_q), .T(1'b1), .Q(t_ff_2_q), .Qn(P1), .preset(Reset_out));  // open: reset, en
  or or_3 (or_4_out[1], C1_out, C1);
  ExactlyOne u_C0 (.out(C0_out), .in0(D6), .in1(D4), .in2(D3), .in3(D1), .in4(D0));
  T_Flip_Flop t_ff_3 (.clk(t_ff_2_q), .T(1'b1), .Q(t_ff_3_q), .Qn(P2), .preset(Reset_out));  // open: reset, en
  ROM #(.addrWidth(3), .dataWidth(12)) rom_1 (
    .addr({A2, A1, A0}), .data({D7, D6, D5, D4, C3, D3, D2, D1, C2, D0, C1, C0}));  // open: sel
  or or_4 (or_4_out[0], C0_out, C0);
  TTY #(.cols(8)) tty_1 (.data({6'b011000, multiplexer_1_out[0]}), .clk(clock_1_out), .we(go), .clr(Reset_out));
  T_Flip_Flop t_ff_4 (.clk(t_ff_3_q), .T(1'b1), .Q(t_ff_4_q), .Qn(A0), .preset(Reset_out));  // open: reset, en
  // Probe on {D7, D6, D5, D4, C3, D3, D2, D1, C2, D0, C1, C0}
  T_Flip_Flop t_ff_5 (.clk(t_ff_4_q), .T(1'b1), .Q(t_ff_5_q), .Qn(A1), .preset(Reset_out));  // open: reset, en
  T_Flip_Flop t_ff_6 (.clk(t_ff_5_q), .T(1'b1), .Q(t_ff_6_q), .Qn(A2), .preset(Reset_out));  // open: reset, en
  not not_1 (not_1_out, D7);
  not not_2 (not_2_out, D4);
  Button Reset (.out(Reset_out));
  T_Flip_Flop t_ff_7 (.clk(t_ff_6_q), .T(1'b1), .Q(go), .preset(Reset_out));  // open: Qn, reset, en
  not not_3 (not_3_out, D5);
  not not_4 (not_4_out, D6);
  Decoder #(.select(4)) decoder_1 (
    .out4(decoder_1_out4), .out5(decoder_1_out5), .out6(decoder_1_out6), .out7(decoder_1_out7),
    .out9(decoder_1_out9), .out11(decoder_1_out11), .out14(decoder_1_out14), .out15(decoder_1_out15),
    .sel(or_4_out));  // open: out0, out1, out2, out3, out8, out10, out12, out13, en
  not not_5 (not_5_out, D2);
  Multiplexer multiplexer_2 (.in0(D7), .in1(not_1_out), .out(Z7), .sel(decoder_1_out9));  // open: en
  not not_6 (not_6_out, D3);
  Multiplexer multiplexer_3 (.in0(D5), .in1(not_3_out), .out(Z5), .sel(decoder_1_out11));  // open: en
  Multiplexer multiplexer_4 (.in0(D4), .in1(not_2_out), .out(Z4), .sel(decoder_1_out7));  // open: en
  Multiplexer multiplexer_5 (.in0(D6), .in1(not_4_out), .out(Z6), .sel(decoder_1_out14));  // open: en
  Multiplexer multiplexer_6 (.in0(D3), .in1(not_6_out), .out(Z3), .sel(decoder_1_out6));  // open: en
  not not_7 (not_7_out, D1);
  Multiplexer multiplexer_7 (.in0(D2), .in1(not_5_out), .out(Z2), .sel(decoder_1_out5));  // open: en
  not not_8 (not_8_out, D0);
  Multiplexer multiplexer_8 (.in0(D1), .in1(not_7_out), .out(Z1), .sel(decoder_1_out15));  // open: en
  Multiplexer multiplexer_9 (.in0(D0), .in1(not_8_out), .out(Z0), .sel(decoder_1_out4));  // open: en

  // Notes on the sheet:
  //   contents of rom_1 (hex, n*v repeats v):
  //   d7 788 a75 a74 275 b75 f75 a77
  //   00101011
  //   01110000
  //   10101111
  //   10101111
  //   10101111
  //   10101111
  //   11111111
  //   10101111
endmodule
