// Logisim project 8.circ as structural Verilog: 3 circuits, main circuit main
module main (
  input  A0,
  input  B0,
  input  Cin,
  input  in_4,
  input  in_5,
  input  A1,
  input  B1,
  input  Cin1,
  input  in_9,
  input  in_10,
  input  A2,
  input  B2,
  input  Cin2,
  input  in_14,
  input  in_15,
  input  A3,
  input  B3,
  input  Cin3,
  input  in_19,
  input  in_20,
  output out_21,
  output Cout,
  output out_23,
  output Cout_2,
  output out_25,
  output Cout_3,
  output out_27,
  output Cout_4
);

  wire adder_1_s, adder_2_s, adder_3_s, adder_4_s, and_1_out, and_2_out, and_3_out, and_4_out, not_1_out,
       not_2_out, not_3_out, not_4_out, or_1_out, or_2_out, or_3_out, or_4_out;

  or or_1 (or_1_out, A0, B0);
  or or_2 (or_2_out, A1, B1);
  or or_3 (or_3_out, A2, B2);
  or or_4 (or_4_out, A3, B3);
  and and_1 (and_1_out, A0, B0);
  adder adder_1 (.A(and_1_out), .B(A0), .Cin(B0), .And(Cin), .S(adder_1_s), .Cout(Cout));
  and and_2 (and_2_out, A1, B1);
  adder adder_2 (.A(and_2_out), .B(A1), .Cin(B1), .And(Cin1), .S(adder_2_s), .Cout(Cout_2));
  and and_3 (and_3_out, A2, B2);
  adder adder_3 (.A(and_3_out), .B(A2), .Cin(B2), .And(Cin2), .S(adder_3_s), .Cout(Cout_3));
  and and_4 (and_4_out, A3, B3);
  adder adder_4 (.A(and_4_out), .B(A3), .Cin(B3), .And(Cin3), .S(adder_4_s), .Cout(Cout_4));
  not not_1 (not_1_out, A0);
  not not_2 (not_2_out, A1);
  not not_3 (not_3_out, A2);
  not not_4 (not_4_out, A3);
  Multiplexer #(.select(2)) multiplexer_1 (
    .in0(not_3_out), .in1(and_3_out), .in2(adder_3_s), .in3(or_3_out), .out(out_25), .sel({in_14, in_15}));  // open: en
  Multiplexer #(.select(2)) multiplexer_2 (
    .in0(not_1_out), .in1(and_1_out), .in2(adder_1_s), .in3(or_1_out), .out(out_21), .sel({in_4, in_5}));  // open: en
  Multiplexer #(.select(2)) multiplexer_3 (
    .in0(not_2_out), .in1(and_2_out), .in2(adder_2_s), .in3(or_2_out), .out(out_23), .sel({in_9, in_10}));  // open: en
  Multiplexer #(.select(2)) multiplexer_4 (
    .in0(not_4_out), .in1(and_4_out), .in2(adder_4_s), .in3(or_4_out), .out(out_27), .sel({in_19, in_20}));  // open: en
endmodule

module adder (
  input  A,
  input  B,
  input  Cin,
  input  And,
  output S,
  output Cout
);

  wire and_1_out, xor_1_out;

  xor xor_1 (xor_1_out, A, B);
  xor xor_2 (S, xor_1_out, Cin);
  and and_1 (and_1_out, xor_1_out, Cin);
  or or_1 (Cout, and_1_out, And);
endmodule

module CLA (
  input  p2,
  input  g2,
  input  p1,
  input  g1,
  input  p0,
  input  g0,
  input  c0,
  output c2,
  output c1
);

  wire nand_3_out, nand_4_out, nand_5_out, not_1_out, not_2_out;

  not not_1 (not_1_out, g1);
  not not_2 (not_2_out, g0);
  // NAND_Gate nand_1 has open pins: in0=p1, in1=g0, out=open
  // NAND_Gate nand_2 has open pins: in0=p2, in1=g1, out=open
  nand nand_3 (nand_3_out, p1, g0);
  nand nand_4 (nand_4_out, p0, c0);
  nand nand_5 (nand_5_out, p0, c0);
  nand nand_6 (c2, not_1_out, nand_3_out, nand_4_out);
  nand nand_7 (c1, not_2_out, nand_5_out);
endmodule
