// Logisim project 1.circ as structural Verilog: 1 circuit, main circuit main
module main (
);

  wire _15, _30, CLOCK, clock_1_out, counter_3_carry, d_ff_1_q, d_ff_1_qn, d_ff_2_qn, d_ff_3_qn, not_1_out,
       Reset_out;
  wire [7:0] counter_1_q, counter_2_q;

  D_Flip_Flop d_ff_1 (.clk(CLOCK), .D(d_ff_1_qn), .Q(d_ff_1_q), .Qn(d_ff_1_qn));  // open: preset, en, reset
  D_Flip_Flop #(.trigger("falling")) d_ff_2 (
    .clk(CLOCK), .D(d_ff_2_qn), .Q(_30), .Qn(d_ff_2_qn));  // open: preset, en, reset
  D_Flip_Flop d_ff_3 (.clk(d_ff_1_q), .D(d_ff_3_qn), .Q(_15), .Qn(d_ff_3_qn));  // open: preset, en, reset
  // Probe on counter_1_q
  Counter counter_1 (.Q(counter_1_q), .clk(_30));  // open: load, D, count, carry, clr
  and and_1 (CLOCK, clock_1_out, not_1_out);
  Clock clock_1 (.out(clock_1_out));
  // Probe on counter_2_q
  Counter counter_2 (.Q(counter_2_q), .clk(_15));  // open: load, D, count, carry, clr
  Counter counter_3 (.carry(counter_3_carry), .clk(CLOCK), .clr(Reset_out));  // open: load, D, count, Q
  not not_1 (not_1_out, counter_3_carry);
  Button Reset (.out(Reset_out));

  // Notes on the sheet:
  //   1 0 0 0 00 0 0
  //   0 1 0 0 0 0 0 0
endmodule
