// Logisim project 4.circ as structural Verilog: 2 circuits, main circuit main
module main (
);

  wire and_1_out, and_2_out, and_3_out, Carry, CLK, clock_1_out, counter_1_carry, D0, D1, D2, D3, Enable,
       Load, multiplexer_1_out, multiplexer_2_out, multiplexer_3_out, multiplexer_4_out, my_xor_1_out_3,
       my_xor_2_out_3, my_xor_3_out_3, my_xor_4_out_3, my_xor_5_out_3, my_xor_6_out_3, my_xor_7_out_3,
       my_xor_8_out_3, not_1_out, Q0, Q1, Q2, Q3;
  wire [5:1] counter_1_q;

  and and_1 (and_1_out, Enable, Q0);
  and and_2 (and_2_out, and_1_out, Q1);
  and and_3 (and_3_out, and_2_out, Q2);
  and and_4 (Carry, and_3_out, Q3);
  Counter #(.width(6), .max('h24)) counter_1 (
    .Q({counter_1_q[5], Load, D3, counter_1_q[2:1], D0}), .carry(counter_1_carry), .clk(CLK));  // open: load, D, count, clr
  and and_5 (CLK, clock_1_out, not_1_out);
  Clock clock_1 (.out(clock_1_out));
  My_XOR my_xor_1 (.A(Q0), .B(Enable), .out_3(my_xor_1_out_3));
  My_XOR my_xor_2 (.A(Q2), .B(and_2_out), .out_3(my_xor_2_out_3));
  TTY #(.rows(1), .cols(37)) tty_1 (.data({2'b10, Carry, Q3, Q2, Q1, Q0}), .clk(CLK));  // open: we, clr
  not not_1 (not_1_out, counter_1_carry);
  My_XOR my_xor_3 (.A(Q1), .B(and_1_out), .out_3(my_xor_3_out_3));
  My_XOR my_xor_4 (.A(Q3), .B(and_3_out), .out_3(my_xor_4_out_3));
  not not_2 (Enable, counter_1_q[5]);
  Multiplexer multiplexer_1 (.in0(my_xor_1_out_3), .in1(D0), .out(multiplexer_1_out), .sel(Load));  // open: en
  Multiplexer multiplexer_2 (.in0(my_xor_3_out_3), .in1(D1), .out(multiplexer_2_out), .sel(Load));  // open: en
  Multiplexer multiplexer_3 (.in0(my_xor_2_out_3), .in1(D2), .out(multiplexer_3_out), .sel(Load));  // open: en
  Multiplexer multiplexer_4 (.in0(my_xor_4_out_3), .in1(D3), .out(multiplexer_4_out), .sel(Load));  // open: en
  or or_1 (D1, Enable, counter_1_q[1]);
  or or_2 (D2, counter_1_q[2], Load);
  My_XOR my_xor_5 (.A(Q0), .B(multiplexer_1_out), .out_3(my_xor_5_out_3));
  My_XOR my_xor_6 (.A(Q1), .B(multiplexer_2_out), .out_3(my_xor_6_out_3));
  My_XOR my_xor_7 (.A(Q2), .B(multiplexer_3_out), .out_3(my_xor_7_out_3));
  My_XOR my_xor_8 (.A(Q3), .B(multiplexer_4_out), .out_3(my_xor_8_out_3));
  T_Flip_Flop t_ff_1 (.clk(CLK), .T(my_xor_5_out_3), .Q(Q0));  // open: Qn, preset, reset, en
  T_Flip_Flop t_ff_2 (.clk(CLK), .T(my_xor_6_out_3), .Q(Q1));  // open: Qn, preset, reset, en
  T_Flip_Flop t_ff_3 (.clk(CLK), .T(my_xor_7_out_3), .Q(Q2));  // open: Qn, preset, reset, en
  T_Flip_Flop t_ff_4 (.clk(CLK), .T(my_xor_8_out_3), .Q(Q3));  // open: Qn, preset, reset, en

  // Notes on the sheet:
  //   @ABCDEFGHIJKLMN_@FGFGFGFGN_N_N_N0000
endmodule

module My_XOR (
  input  A,
  input  B,
  output out_3
);

  wire and_1_out, and_2_out, not_1_out, not_2_out;

  not not_1 (not_1_out, A);
  not not_2 (not_2_out, B);
  and and_1 (and_1_out, A, not_2_out);
  and and_2 (and_2_out, not_1_out, B);
  or or_1 (out_3, and_1_out, and_2_out);
endmodule
