// Logisim project 8.circ as structural Verilog: 1 circuit, main circuit main
module main (
);

  wire _4_Counter_carry, and_1_out, and_2_out, and_3_out, and_4_out, and_5_out, and_6_out, and_7_out,
       and_8_out, and_9_out, and_10_out, CLK, clock_1_out, d_ff_1_qn, d_ff_2_qn, d_ff_3_qn, go, I5, I10, I25,
       not_1_out, not_2_out, not_3_out, O5, O10, OM, or_1_out, or_2_out, or_3_out, Reset_out;
  wire [4:0] _4_Counter_q;

  D_Flip_Flop d_ff_1 (.clk(CLK), .D(or_1_out), .Q(O5), .Qn(d_ff_1_qn));  // open: preset, en, reset
  D_Flip_Flop d_ff_2 (.clk(CLK), .D(or_2_out), .Q(O10), .Qn(d_ff_2_qn));  // open: preset, en, reset
  D_Flip_Flop d_ff_3 (.clk(CLK), .D(or_3_out), .Q(OM), .Qn(d_ff_3_qn));  // open: preset, en, reset
  not not_1 (not_1_out, I5);
  not not_2 (not_2_out, I10);
  and and_1 (and_1_out, I5, d_ff_1_qn, d_ff_2_qn, d_ff_3_qn);
  and and_2 (and_2_out, I10, d_ff_1_qn, O10, d_ff_3_qn);
  and and_3 (and_3_out, d_ff_1_qn, O10, not_1_out, not_2_out, not_3_out);
  and and_4 (and_4_out, d_ff_1_qn, d_ff_2_qn, OM, I25);
  and and_5 (and_5_out, d_ff_1_qn, O10, d_ff_3_qn, not_1_out, I25);
  and and_6 (and_6_out, d_ff_1_qn, d_ff_2_qn, d_ff_3_qn, not_1_out);
  and and_7 (and_7_out, not_2_out, d_ff_1_qn, OM, not_1_out, not_3_out);
  and and_8 (and_8_out, d_ff_1_qn, d_ff_2_qn, OM, I10);
  and and_9 (and_9_out, d_ff_1_qn, O10, OM, not_1_out, I10);
  not not_3 (not_3_out, I25);
  and and_10 (and_10_out, I25, not_1_out, d_ff_1_qn, O10, OM);
  or or_1 (or_1_out, and_10_out, and_1_out, and_2_out);
  or or_2 (or_2_out, and_3_out, and_4_out, and_5_out);
  or or_3 (or_3_out, and_6_out, and_7_out, and_8_out, and_9_out);
  TTY #(.rows(1), .cols(33)) tty_1 (.data({4'b1000, OM, O10, O5}), .clk(CLK), .we(go), .clr(Reset_out));
  Button Reset (.out(Reset_out));
  Counter #(.width(5), .max('h1f)) _4_Counter (
    .Q(_4_Counter_q), .carry(_4_Counter_carry), .clk(CLK), .clr(Reset_out));  // open: load, D, count
  and and_11 (CLK, clock_1_out, go);
  Clock clock_1 (.out(clock_1_out));
  // Probe on _4_Counter_q
  not not_4 (go, _4_Counter_carry);
  // Probe on I5
  // Probe on I10
  ROM #(.addrWidth(5), .dataWidth(3)) rom_1 (.addr(_4_Counter_q), .data({I25, I10, I5}));  // open: sel
  // Probe on I25

  // Notes on the sheet:
  //   24 Gates
  //   D@@@@D@@@D@@E@E@F@@G@@G@F@@E@@@
  //   contents of rom_1 (hex, n*v repeats v):
  //   4 6*1 2 1 1 2 2 2 1 4 2 4 2 2 4 1 2 4 2 4 2 2 2 1 1 1 2
endmodule
