// Logisim project ALU.circ as structural Verilog: 3 circuits, main circuit main
module main (
  input  Cin,
  input  A0,
  input  B0,
  input  A1,
  input  B1,
  input  A2,
  input  B2,
  input  A3,
  input  B3,
  input  S4,
  input  S3,
  input  S2,
  input  S1,
  output C0,
  output C1,
  output C4,
  output C2,
  output C3
);

  wire Add0, Add1, Add2, Add3, ADD_2_out, ADD_3_out, ADD_4_out, ADD_5_out, ADD_out, ADDI_2_out, ADDI_3_out,
       ADDI_4_out, ADDI_5_out, ADDI_out, AND_2_out, AND_3_out, AND_4_out, AND_5_out, and_6_out, and_7_out,
       and_8_out, and_9_out, and_10_out, and_11_out, and_12_out, and_13_out, and_14_out, and_15_out, AND_out,
       C1out, C2out, C3out, G0, G1, G2, G3, MOV_2_out, MOV_3_out, MOV_4_out, MOV_5_out, MOV_out, MOVI_2_out,
       MOVI_3_out, MOVI_4_out, MOVI_5_out, MOVI_out, not_1_out, not_2_out, not_3_out, not_4_out, not_5_out,
       not_6_out, not_7_out, not_8_out, NOT_9_out, NOT_10_out, NOT_11_out, NOT_12_out, NOT_13_out,
       not_14_out, or_2_out, or_3_out, or_4_out, or_5_out, OR_6_out, OR_7_out, OR_8_out, OR_9_out, OR_out,
       P0, P1, P2, P3, SLL_2_out, SLL_3_out, SLL_4_out, SLL_5_out, SLL_out, SRL_3_out, SRL_4_out, SRL_5_out,
       SRL_out, SUB0, SUB1, SUB2, SUB3, SUB_2_out, SUB_3_out, SUB_4_out, SUB_5_out, SUB_out, SUBI_2_out,
       SUBI_3_out, SUBI_4_out, SUBI_5_out, SUBI_out;

  not not_1 (not_1_out, S4);
  not not_2 (not_2_out, S3);
  not not_3 (not_3_out, S2);
  not not_4 (not_4_out, S1);
  not not_5 (not_5_out, A0);
  not not_6 (not_6_out, A1);
  not not_7 (not_7_out, A2);
  not not_8 (not_8_out, A3);
  and AND (AND_out, not_1_out, not_2_out, not_3_out, not_4_out);
  and OR (OR_out, not_1_out, not_2_out, not_3_out, S1);
  and NOT_9 (NOT_9_out, not_1_out, not_2_out, S2, not_4_out);
  and ADD (ADD_out, not_1_out, not_2_out, S2, S1);
  and MOV (MOV_out, not_1_out, S3, not_3_out, not_4_out);
  and SLL (SLL_out, not_1_out, S3, not_3_out, S1);
  and SRL (SRL_out, not_1_out, S3, S2, not_4_out);
  and SUB (SUB_out, not_1_out, S3, S2, S1);
  and ADDI (ADDI_out, S4, not_2_out, not_3_out, not_4_out);
  and SUBI (SUBI_out, S4, not_2_out, not_3_out, S1);
  and MOVI (MOVI_out, S4, not_2_out, S2, not_4_out);
  Adder adder_1 (.A(A0), .B(B0), .Cin(Cin), .P(P0), .G(G0), .S(Add0));  // open: Cout
  and AND_2 (AND_2_out, A0, B0, AND_out);
  or or_2 (or_2_out, A0, B0);
  and NOT_10 (NOT_10_out, not_5_out, OR_out);
  and MOV_2 (MOV_2_out, A0, MOV_out);
  and SLL_2 (SLL_2_out, A0, SLL_out);
  // AND_Gate SRL_2 has open pins: in0=A0, in1=SRL_out, out=open
  and SUB_2 (SUB_2_out, SUB0, SUB_out);
  and ADDI_2 (ADDI_2_out, Add0, ADDI_out);
  and SUBI_2 (SUBI_2_out, SUB0, SUBI_out);
  and MOVI_2 (MOVI_2_out, B0, MOVI_out);
  Adder adder_2 (.A(A1), .B(B1), .Cin(C1out), .P(P1), .G(G1), .S(Add1));  // open: Cout
  and AND_3 (AND_3_out, A1, B1, AND_out);
  or or_3 (or_3_out, A1, B1);
  and NOT_11 (NOT_11_out, not_6_out, OR_out);
  and MOV_3 (MOV_3_out, A1, MOV_out);
  and SLL_3 (SLL_3_out, A1, SLL_out);
  and SRL_3 (SRL_3_out, A1, SRL_out);
  and SUB_3 (SUB_3_out, SUB1, SUB_out);
  and ADDI_3 (ADDI_3_out, Add1, ADDI_out);
  and SUBI_3 (SUBI_3_out, SUB1, SUBI_out);
  and MOVI_3 (MOVI_3_out, B1, MOVI_out);
  Adder adder_3 (.A(A2), .B(B2), .Cin(C2out), .P(P2), .G(G2), .S(Add2));  // open: Cout
  and AND_4 (AND_4_out, A2, B2, AND_out);
  or or_4 (or_4_out, A2, B2);
  and NOT_12 (NOT_12_out, not_7_out, OR_out);
  and MOV_4 (MOV_4_out, A2, MOV_out);
  and SLL_4 (SLL_4_out, A2, SLL_out);
  and SRL_4 (SRL_4_out, A2, SRL_out);
  and SUB_4 (SUB_4_out, SUB2, SUB_out);
  and ADDI_4 (ADDI_4_out, Add2, ADDI_out);
  and SUBI_4 (SUBI_4_out, SUB2, SUBI_out);
  and MOVI_4 (MOVI_4_out, B2, MOVI_out);
  Adder adder_4 (.A(A3), .B(B3), .Cin(C3out), .P(P3), .G(G3), .S(Add3));  // open: Cout
  and AND_5 (AND_5_out, A3, B3, AND_out);
  or or_5 (or_5_out, A3, B3);
  and NOT_13 (NOT_13_out, not_8_out, OR_out);
  and MOV_5 (MOV_5_out, A3, MOV_out);
  and SLL_5 (SLL_5_out, A3, SLL_out);
  and SRL_5 (SRL_5_out, A3, SRL_out);
  and SUB_5 (SUB_5_out, SUB3, SUB_out);
  and ADDI_5 (ADDI_5_out, Add3, ADDI_out);
  and SUBI_5 (SUBI_5_out, SUB3, SUBI_out);
  and MOVI_5 (MOVI_5_out, B3, MOVI_out);
  and ADD_2 (ADD_2_out, Add0, ADD_out);
  and OR_6 (OR_6_out, or_2_out, NOT_9_out);
  and OR_7 (OR_7_out, or_3_out, NOT_9_out);
  and OR_8 (OR_8_out, or_4_out, NOT_9_out);
  and OR_9 (OR_9_out, or_5_out, NOT_9_out);
  and ADD_3 (ADD_3_out, Add1, ADD_out);
  and ADD_4 (ADD_4_out, ADD_out, Add2);
  and ADD_5 (ADD_5_out, Add3, ADD_out);
  or or_10 (C0, ADD_2_out, AND_2_out, OR_6_out, NOT_10_out, MOV_2_out, SRL_3_out, SUB_2_out, ADDI_2_out, SUBI_2_out, MOVI_2_out);
  or or_11 (C1, ADD_3_out, AND_3_out, OR_7_out, NOT_11_out, MOV_3_out, SLL_2_out, SRL_4_out, SUB_3_out, ADDI_3_out, SUBI_3_out, MOVI_3_out);
  or or_12 (C2, ADD_4_out, AND_4_out, OR_8_out, NOT_12_out, MOV_4_out, SLL_3_out, SRL_5_out, SUB_4_out, ADDI_4_out, SUBI_4_out, MOVI_4_out);
  or or_13 (C3, ADD_5_out, AND_5_out, OR_9_out, NOT_13_out, MOV_5_out, SLL_4_out, SUB_5_out, ADDI_5_out, SUBI_5_out, MOVI_5_out);
  not not_14 (not_14_out, Cin);
  Subtracter subtracter_1 (.B(B0), .A(A0), .Cin(not_14_out), .S(SUB0));  // open: Cout
  Subtracter subtracter_2 (.B(B1), .A(A1), .Cin(C1out), .S(SUB1));  // open: Cout
  Subtracter subtracter_3 (.B(B2), .A(A2), .Cin(C2out), .S(SUB2));  // open: Cout
  Subtracter subtracter_4 (.B(B3), .A(A3), .Cin(C3out), .S(SUB3));  // open: Cout
  and and_6 (and_6_out, Cin, P0);
  and and_7 (and_7_out, Cin, P1, P0);
  and and_8 (and_8_out, G0, P1);
  and and_9 (and_9_out, Cin, P0, P1, P2);
  and and_10 (and_10_out, P1, P2, G0);
  and and_11 (and_11_out, P2, G1);
  and and_12 (and_12_out, Cin, P3, P2, P1, P0);
  and and_13 (and_13_out, G0, P1, P2, P3);
  and and_14 (and_14_out, G1, P2, P3);
  and and_15 (and_15_out, G2, P3);
  or or_14 (C1out, and_6_out, G0);
  or or_15 (C2out, and_7_out, and_8_out, G1);
  or or_16 (C3out, and_9_out, and_10_out, and_11_out, G2);
  or or_17 (C4, and_12_out, and_13_out, and_14_out, and_15_out, G3);
endmodule

module Adder (
  input  A,
  input  B,
  input  Cin,
  output P,
  output S,
  output Cout,
  output G
);

  wire and_2_out;

  xor xor_1 (P, A, B);
  and and_1 (G, A, B);
  xor xor_2 (S, P, Cin);
  and and_2 (and_2_out, P, Cin);
  or or_1 (Cout, and_2_out, G);
endmodule

module Subtracter (
  input  B,
  input  A,
  input  Cin,
  output S,
  output Cout
);

  wire and_1_out, and_2_out, not_1_out, not_2_out, xor_1_out;

  not not_1 (not_1_out, B);
  xor xor_1 (xor_1_out, B, A);
  and and_1 (and_1_out, A, not_1_out);
  not not_2 (not_2_out, xor_1_out);
  xor xor_2 (S, xor_1_out, Cin);
  and and_2 (and_2_out, not_2_out, Cin);
  or or_1 (Cout, and_2_out, and_1_out);
endmodule
