// Logisim project cpu.circ as structural Verilog: 6 circuits, main circuit main
// I8
module main (
  input  in_1,
  input  in_2,
  output [7:0] out_3,
  output [7:0] out_4,
  output [7:0] out_5,
  output [7:0] out_6,
  output [7:0] out_7,
  output [7:0] out_8,
  output [7:0] out_9,
  output [7:0] out_10,
  output [7:0] out_11
);

  wire alu_2_c4, and_1_out, and_2_out, and_4_out, and_5_out, and_6_out, and_7_out, clock_1_out,
       comparator_1_lt, comparator_2_lt, counter_1_carry, decoder_1_out0, decoder_1_out1, decoder_1_out2,
       decoder_1_out3, decoder_1_out4, decoder_1_out5, decoder_1_out6, decoder_1_out7, decoder_1_out8, I,
       not_1_out, not_2_out, not_3_out, not_4_out, Reset, TClock, undriven;
  wire [3:0] B, D, multiplexer_4_out, multiplexer_4_out_2, multiplexer_5_out, multiplexer_5_out_2,
       rom_1_data, S;
  wire [4:0] counter_1_q, t_ff_1_q;
  wire [6:0] adder_1_out, adder_2_out, LSB, MSB;
  wire [7:0] multiplexer_1_out, Write;
  wire [7:4] Data;
  wire [19:12] ram_1_data;

  T_Flip_Flop t_ff_1 (.clk(TClock), .T(not_1_out), .Q(t_ff_1_q[0]), .en(not_3_out));  // open: Qn, preset, reset
  not not_1 (not_1_out, in_1);
  T_Flip_Flop t_ff_2 (.clk(TClock), .T(t_ff_1_q[0]), .Q(t_ff_1_q[1]), .en(not_3_out));  // open: Qn, preset, reset
  TTY #(.rows(33), .cols(1)) tty_1 (.data(MSB), .clk(TClock), .clr(Reset));  // open: we
  TTY #(.rows(33), .cols(1)) tty_2 (.data(LSB), .clk(TClock), .clr(Reset));  // open: we
  T_Flip_Flop t_ff_3 (.clk(TClock), .T(and_1_out), .Q(t_ff_1_q[2]), .en(not_3_out));  // open: Qn, preset, reset
  and and_1 (and_1_out, t_ff_1_q[1], t_ff_1_q[0]);
  Counter #(.width(5), .max('h1f)) counter_1 (
    .Q(counter_1_q), .carry(counter_1_carry), .clk(TClock), .clr(Reset));  // open: load, D, count
  and and_2 (and_2_out, and_1_out, t_ff_1_q[2]);
  Button u_Reset (.out(Reset));
  Multiplexer #(.select(4), .width(8), .disabled(0), .enable("false")) multiplexer_1 (
    .in0(out_3), .in1(out_4), .in2(out_5), .in3(out_6), .in4(out_7), .in5(out_8), .in6(out_9), .in7(out_10),
    .in8(out_11), .out(multiplexer_1_out), .sel(rom_1_data));  // open: in9, in10, in11, in12, in13, in14, in15
  not not_2 (not_2_out, counter_1_carry);
  Clock clock_1 (.out(clock_1_out));
  T_Flip_Flop t_ff_4 (.clk(TClock), .T(and_2_out), .Q(t_ff_1_q[3]), .en(not_3_out));  // open: Qn, preset, reset
  RAM #(.addrWidth(5), .dataWidth(24)) ram_1 (
    .addr(t_ff_1_q), .data({S, ram_1_data, B, Data, D}), .clk(TClock), .ld(undriven));  // open: sel, clr
  not not_3 (not_3_out, and_5_out);
  and and_3 (TClock, not_2_out, clock_1_out);
  and and_4 (and_4_out, t_ff_1_q[3], and_2_out);
  and and_5 (and_5_out, S[0], S[1], S[2], S[3]);
  Comparator #(.width(7)) comparator_1 (
    .a(7'b0111001), .b({3'b011, multiplexer_1_out[3:0]}), .lt(comparator_1_lt));  // open: gt, eq
  Comparator #(.width(7)) comparator_2 (
    .a(7'b0111001), .b({3'b011, multiplexer_1_out[7:4]}), .lt(comparator_2_lt));  // open: gt, eq
  ROM #(.addrWidth(5), .dataWidth(4)) rom_1 (.addr(counter_1_q), .data(rom_1_data));  // open: sel
  T_Flip_Flop t_ff_5 (.clk(TClock), .T(and_4_out), .Q(t_ff_1_q[4]), .en(not_3_out));  // open: Qn, preset, reset
  Decoder #(.select(4)) decoder_1 (
    .out0(decoder_1_out0), .out1(decoder_1_out1), .out2(decoder_1_out2), .out3(decoder_1_out3),
    .out4(decoder_1_out4), .out5(decoder_1_out5), .out6(decoder_1_out6), .out7(decoder_1_out7),
    .out8(decoder_1_out8), .sel(ram_1_data[19:16]));  // open: out9, out10, out11, out12, out13, out14, out15, en
  not not_4 (not_4_out, S[2]);
  and and_6 (and_6_out, S[3], not_4_out, S[1], S[0]);
  not not_5 (I, and_6_out);
  Multiplexer #(.width(7), .disabled(0), .enable("false")) multiplexer_2 (
    .in0({3'b011, multiplexer_1_out[3:0]}), .in1(adder_1_out), .out(LSB), .sel(comparator_1_lt));
  Adder_part #(.width(7)) adder_1 (
    .a({3'b011, multiplexer_1_out[3:0]}), .b(7'b0000111), .out(adder_1_out));  // open: cin, cout
  Multiplexer #(.width(7), .disabled(0), .enable("false")) multiplexer_3 (
    .in0({3'b011, multiplexer_1_out[7:4]}), .in1(adder_2_out), .out(MSB), .sel(comparator_2_lt));
  Adder_part #(.width(7)) adder_2 (
    .a({3'b011, multiplexer_1_out[7:4]}), .b(7'b0000111), .out(adder_2_out));  // open: cin, cout
  register_bank register_bank_1 (
    .decoders(and_7_out), .in_3(decoder_1_out1), .in_4(decoder_1_out2), .in_5(decoder_1_out3),
    .in_6(decoder_1_out4), .in_7(decoder_1_out5), .in_8(decoder_1_out6), .in_9(decoder_1_out7),
    .in_10(decoder_1_out8), .CLOCK(TClock), .ALU(Write),
    .R0({out_3[0], out_3[1], out_3[2], out_3[3], out_3[4], out_3[5], out_3[6], out_3[7]}),
    .R1({out_4[0], out_4[1], out_4[2], out_4[3], out_4[4], out_4[5], out_4[6], out_4[7]}),
    .R2({out_5[0], out_5[1], out_5[2], out_5[3], out_5[4], out_5[5], out_5[6], out_5[7]}),
    .R3({out_6[0], out_6[1], out_6[2], out_6[3], out_6[4], out_6[5], out_6[6], out_6[7]}),
    .R4({out_7[0], out_7[1], out_7[2], out_7[3], out_7[4], out_7[5], out_7[6], out_7[7]}),
    .R5({out_8[0], out_8[1], out_8[2], out_8[3], out_8[4], out_8[5], out_8[6], out_8[7]}),
    .R6({out_9[0], out_9[1], out_9[2], out_9[3], out_9[4], out_9[5], out_9[6], out_9[7]}),
    .R7({out_10[0], out_10[1], out_10[2], out_10[3], out_10[4], out_10[5], out_10[6], out_10[7]}),
    .R8({out_11[0], out_11[1], out_11[2], out_11[3], out_11[4], out_11[5], out_11[6], out_11[7]}));
  and and_7 (and_7_out, I, decoder_1_out0);
  Multiplexer #(.select(4), .width(8)) multiplexer_4 (
    .in0(out_3), .in1(out_4), .in2(out_5), .in3(out_6), .in4(out_7), .in5(out_8), .in6(out_9), .in7(out_10),
    .in8(out_11), .out({multiplexer_4_out_2, multiplexer_4_out}), .sel(ram_1_data[15:12]));  // open: in9, in10, in11, in12, in13, in14, in15, en
  ALU alu_1 (
    .Cin(alu_2_c4), .A(multiplexer_4_out_2), .B(multiplexer_5_out_2), .D(Data), .S(S), .out_7(Write[7:4]));  // open: in_6, C4
  ALU alu_2 (
    .Cin(in_2), .A(multiplexer_4_out), .B(multiplexer_5_out), .D(D), .S(S), .out_7(Write[3:0]), .C4(alu_2_c4));  // open: in_6
  Multiplexer #(.select(4), .width(8)) multiplexer_5 (
    .in0(out_3), .in1(out_4), .in2(out_5), .in3(out_6), .in4(out_7), .in5(out_8), .in6(out_9), .in7(out_10),
    .in8(out_11), .in9({Data, D}), .out({multiplexer_5_out_2, multiplexer_5_out}), .sel(B));  // open: in10, in11, in12, in13, in14, in15, en

  // Other names for the same wires on the sheet: Data[3:0] = D; R0[7:0] = out_3;
  //   R0Fix[7:0] = {out_3[0], out_3[1], out_3[2], out_3[3], out_3[4], out_3[5], out_3[6], out_3[7]};
  //   R0Fixed[7:0] = out_3; R1[7:0] = out_4;
  //   R1Fix[7:0] = {out_4[0], out_4[1], out_4[2], out_4[3], out_4[4], out_4[5], out_4[6], out_4[7]};
  //   R1Fixed[7:0] = out_4; R2[7:0] = out_5;
  //   R2Fix[7:0] = {out_5[0], out_5[1], out_5[2], out_5[3], out_5[4], out_5[5], out_5[6], out_5[7]};
  //   R2Fixed[7:0] = out_5; R3[7:0] = out_6;
  //   R3Fix[7:0] = {out_6[0], out_6[1], out_6[2], out_6[3], out_6[4], out_6[5], out_6[6], out_6[7]};
  //   R3Fixed[7:0] = out_6; R4[7:0] = out_7;
  //   R4Fix[7:0] = {out_7[0], out_7[1], out_7[2], out_7[3], out_7[4], out_7[5], out_7[6], out_7[7]};
  //   R4Fixed[7:0] = out_7; R5[7:0] = out_8;
  //   R5Fix[7:0] = {out_8[0], out_8[1], out_8[2], out_8[3], out_8[4], out_8[5], out_8[6], out_8[7]};
  //   R5Fixed[7:0] = out_8; R6[7:0] = out_9;
  //   R6Fix[7:0] = {out_9[0], out_9[1], out_9[2], out_9[3], out_9[4], out_9[5], out_9[6], out_9[7]};
  //   R6Fixed[7:0] = out_9; R7[7:0] = out_10;
  //   R7Fix[7:0] = {out_10[0], out_10[1], out_10[2], out_10[3], out_10[4], out_10[5], out_10[6], out_10[7]};
  //   R7Fixed[7:0] = out_10; R8[7:0] = out_11;
  //   R8Fix[7:0] = {out_11[0], out_11[1], out_11[2], out_11[3], out_11[4], out_11[5], out_11[6], out_11[7]};
  //   R8Fixed[7:0] = out_11

  // Notes on the sheet:
  //   00
  //   F5
  //   5A
  //   50
  //   FF
  //   0A
  //   4F
  //   F5
  //   EA
  //   7A
  //   9B
  //   65
  //   0F
  //   FF
  //   F5
  //   AA
  //   5A
  //   0A
  //   FA
  //   A5
  //   04
  //   5A
  //   B4
  //   2D
  //   0A
  //   B0
  //   50
  //   0F
  //   00
  //   00
  //   5A
  //   contents of rom_1 (hex, n*v repeats v):
  //   0 0 1 2 3 4 5 6 7 8 2 3 4 5 0 0 1 6 7 8 2 3 4 5 6 6 7 8 2 3 4 4
endmodule

module _8_bit_register (
  input  Clock,
  input  in_2,
  input  [7:0] ALU,
  output [7:0] out_4
);

  D_Flip_Flop d_ff_1 (.clk(Clock), .D(ALU[0]), .Q(out_4[7]), .en(in_2));  // open: Qn, preset, reset
  D_Flip_Flop d_ff_2 (.clk(Clock), .D(ALU[1]), .Q(out_4[6]), .en(in_2));  // open: Qn, preset, reset
  D_Flip_Flop d_ff_3 (.clk(Clock), .D(ALU[2]), .Q(out_4[5]), .en(in_2));  // open: Qn, preset, reset
  D_Flip_Flop d_ff_4 (.clk(Clock), .D(ALU[3]), .Q(out_4[4]), .en(in_2));  // open: Qn, preset, reset
  D_Flip_Flop d_ff_5 (.clk(Clock), .D(ALU[4]), .Q(out_4[3]), .en(in_2));  // open: Qn, preset, reset
  D_Flip_Flop d_ff_6 (.clk(Clock), .D(ALU[5]), .Q(out_4[2]), .en(in_2));  // open: Qn, preset, reset
  D_Flip_Flop d_ff_7 (.clk(Clock), .D(ALU[6]), .Q(out_4[1]), .en(in_2));  // open: Qn, preset, reset
  D_Flip_Flop d_ff_8 (.clk(Clock), .D(ALU[7]), .Q(out_4[0]), .en(in_2));  // open: Qn, preset, reset
endmodule

module register_bank (
  input  CLOCK,
  input  decoders,
  input  in_3,
  input  in_4,
  input  in_5,
  input  in_6,
  input  in_7,
  input  in_8,
  input  in_9,
  input  in_10,
  input  [7:0] ALU,
  output [7:0] R0,
  output [7:0] R1,
  output [7:0] R2,
  output [7:0] R3,
  output [7:0] R4,
  output [7:0] R5,
  output [7:0] R6,
  output [7:0] R7,
  output [7:0] R8
);

  _8_bit_register u_8_bit_register_1 (.Clock(CLOCK), .in_2(decoders), .out_4(R0), .ALU(ALU));
  _8_bit_register u_8_bit_register_2 (.Clock(CLOCK), .in_2(in_3), .out_4(R1), .ALU(ALU));
  _8_bit_register u_8_bit_register_3 (.Clock(CLOCK), .in_2(in_4), .out_4(R2), .ALU(ALU));
  _8_bit_register u_8_bit_register_4 (.Clock(CLOCK), .in_2(in_5), .out_4(R3), .ALU(ALU));
  _8_bit_register u_8_bit_register_5 (.Clock(CLOCK), .in_2(in_6), .out_4(R4), .ALU(ALU));
  _8_bit_register u_8_bit_register_6 (.Clock(CLOCK), .in_2(in_7), .out_4(R5), .ALU(ALU));
  _8_bit_register u_8_bit_register_7 (.Clock(CLOCK), .in_2(in_8), .out_4(R6), .ALU(ALU));
  _8_bit_register u_8_bit_register_8 (.Clock(CLOCK), .in_2(in_9), .out_4(R7), .ALU(ALU));
  _8_bit_register u_8_bit_register_9 (.Clock(CLOCK), .in_2(in_10), .out_4(R8), .ALU(ALU));
endmodule

module ALU (
  input  Cin,
  input  [3:0] A,
  input  [3:0] B,
  input  [3:0] D,
  input  [3:0] S,
  input  in_6,
  output [3:0] out_7,
  output C4
);

  wire Add, Add0, Add1, Add2, Add3, ADD_2_out, ADD_3_out, ADD_4_out, ADD_5_out, adder_8_p1, Addi, ADDI_2_out,
       ADDI_3_out, ADDI_4_out, ADDI_5_out, AND_2_out, AND_3_out, AND_4_out, AND_5_out, and_6_out, and_7_out,
       and_8_out, and_9_out, and_10_out, and_11_out, and_12_out, and_13_out, and_14_out, and_15_out,
       and_16_out, and_17_out, and_18_out, and_19_out, and_20_out, and_21_out, and_22_out, and_23_out,
       and_24_out, and_25_out, and_26_out, and_27_out, AND_out, B0, B1, B2, B3, C1out, C1outs, C2out, C2outs,
       C3out, C3outs, C4_t, C4s, G0, G0s, G1, G1s, G2, G2s, G3, G3s, MOV_2_out, MOV_3_out, MOV_4_out,
       MOV_5_out, MOV_out, MOVI_2_out, MOVI_3_out, MOVI_4_out, MOVI_5_out, MOVI_out, not_1_out, not_2_out,
       not_3_out, not_4_out, not_5_out, not_6_out, not_7_out, not_8_out, NOT_9_out, NOT_10_out, NOT_11_out,
       NOT_12_out, NOT_13_out, not_14_out, not_15_out, not_16_out, not_17_out, not_18_out, not_19_out,
       not_20_out, or_2_out, or_3_out, or_4_out, or_5_out, OR_6_out, OR_7_out, OR_8_out, OR_9_out, or_14_out,
       or_16_out, OR_out, P0, P0s, P1, P1s, P2, P2s, P3, P3s, SLL_2_out, SLL_3_out, SLL_4_out, SLL_5_out,
       SLL_out, SRL_3_out, SRL_4_out, SRL_5_out, SRL_out, Sub, SUB0, SUB1, SUB2, SUB3, SUB_2_out, SUB_3_out,
       SUB_4_out, SUB_5_out, Subi, SUBI_2_out, SUBI_3_out, SUBI_4_out, SUBI_5_out;

  not not_1 (not_1_out, S[3]);
  not not_2 (not_2_out, S[2]);
  not not_3 (not_3_out, S[1]);
  not not_4 (not_4_out, S[0]);
  not not_5 (not_5_out, A[0]);
  not not_6 (not_6_out, A[1]);
  not not_7 (not_7_out, A[2]);
  not not_8 (not_8_out, A[3]);
  and AND (AND_out, not_1_out, not_2_out, not_3_out, not_4_out);
  and OR (OR_out, not_1_out, not_2_out, not_3_out, S[0]);
  and NOT_9 (NOT_9_out, not_1_out, not_2_out, S[1], not_4_out);
  and u_ADD (Add, not_1_out, not_2_out, S[1], S[0]);
  and MOV (MOV_out, not_1_out, S[2], not_3_out, not_4_out);
  and SLL (SLL_out, not_1_out, S[2], not_3_out, S[0]);
  and SRL (SRL_out, not_1_out, S[2], S[1], not_4_out);
  and u_SUB (Sub, not_1_out, S[2], S[1], S[0]);
  and u_ADDI (Addi, S[3], not_2_out, not_3_out, not_4_out);
  and u_SUBI (Subi, S[3], not_2_out, not_3_out, S[0]);
  and MOVI (MOVI_out, S[3], not_2_out, S[1], not_4_out);
  Adder adder_1 (.A(A[0]), .B(B0), .Cin(Cin), .P(P0), .G(G0), .S(Add0));  // open: Cout
  and AND_2 (AND_2_out, A[0], B0, AND_out);
  or or_2 (or_2_out, A[0], B0);
  and NOT_10 (NOT_10_out, not_5_out, NOT_9_out);
  and MOV_2 (MOV_2_out, A[0], MOV_out);
  and SLL_2 (SLL_2_out, A[0], SLL_out);
  // AND_Gate SRL_2 has open pins: in0=A[0], in1=SRL_out, out=open
  and SUB_2 (SUB_2_out, SUB0, Sub);
  and ADDI_2 (ADDI_2_out, Add0, Addi);
  and SUBI_2 (SUBI_2_out, SUB0, Subi);
  and MOVI_2 (MOVI_2_out, B0, MOVI_out);
  Adder adder_2 (.A(A[1]), .B(B1), .Cin(C1out), .P(P1), .G(G1), .S(Add1));  // open: Cout
  and AND_3 (AND_3_out, A[1], B1, AND_out);
  or or_3 (or_3_out, A[1], B1);
  and NOT_11 (NOT_11_out, not_6_out, NOT_9_out);
  and MOV_3 (MOV_3_out, A[1], MOV_out);
  and SLL_3 (SLL_3_out, A[1], SLL_out);
  and SRL_3 (SRL_3_out, A[1], SRL_out);
  and SUB_3 (SUB_3_out, SUB1, Sub);
  and ADDI_3 (ADDI_3_out, Add1, Addi);
  and SUBI_3 (SUBI_3_out, SUB1, Subi);
  and MOVI_3 (MOVI_3_out, B1, MOVI_out);
  Adder adder_3 (.A(A[2]), .B(B2), .Cin(C2out), .P(P2), .G(G2), .S(Add2));  // open: Cout
  and AND_4 (AND_4_out, A[2], B2, AND_out);
  or or_4 (or_4_out, A[2], B2);
  and NOT_12 (NOT_12_out, not_7_out, NOT_9_out);
  and MOV_4 (MOV_4_out, A[2], MOV_out);
  and SLL_4 (SLL_4_out, A[2], SLL_out);
  and SRL_4 (SRL_4_out, A[2], SRL_out);
  and SUB_4 (SUB_4_out, SUB2, Sub);
  and ADDI_4 (ADDI_4_out, Add2, Addi);
  and SUBI_4 (SUBI_4_out, SUB2, Subi);
  and MOVI_4 (MOVI_4_out, B2, MOVI_out);
  Adder adder_4 (.A(A[3]), .B(B3), .Cin(C3out), .P(P3), .G(G3), .S(Add3));  // open: Cout
  and AND_5 (AND_5_out, A[3], B3, AND_out);
  or or_5 (or_5_out, A[3], B3);
  and NOT_13 (NOT_13_out, not_8_out, NOT_9_out);
  and MOV_5 (MOV_5_out, A[3], MOV_out);
  and SLL_5 (SLL_5_out, A[3], SLL_out);
  and SRL_5 (SRL_5_out, A[3], SRL_out);
  and SUB_5 (SUB_5_out, SUB3, Sub);
  and ADDI_5 (ADDI_5_out, Add3, Addi);
  and SUBI_5 (SUBI_5_out, SUB3, Subi);
  and MOVI_5 (MOVI_5_out, B3, MOVI_out);
  and ADD_2 (ADD_2_out, Add0, Add);
  and OR_6 (OR_6_out, or_2_out, OR_out);
  and OR_7 (OR_7_out, or_3_out, OR_out);
  and OR_8 (OR_8_out, or_4_out, OR_out);
  and OR_9 (OR_9_out, or_5_out, OR_out);
  and ADD_3 (ADD_3_out, Add1, Add);
  and ADD_4 (ADD_4_out, Add, Add2);
  and ADD_5 (ADD_5_out, Add3, Add);
  or or_10 (out_7[0], ADD_2_out, AND_2_out, OR_6_out, NOT_10_out, MOV_2_out, SRL_3_out, SUB_2_out, ADDI_2_out, SUBI_2_out, MOVI_2_out);
  or or_11 (out_7[1], ADD_3_out, AND_3_out, OR_7_out, NOT_11_out, MOV_3_out, SLL_2_out, SRL_4_out, SUB_3_out, ADDI_3_out, SUBI_3_out, MOVI_3_out);
  or or_12 (out_7[2], ADD_4_out, AND_4_out, OR_8_out, NOT_12_out, MOV_4_out, SLL_3_out, SRL_5_out, SUB_4_out, ADDI_4_out, SUBI_4_out, MOVI_4_out);
  or or_13 (out_7[3], ADD_5_out, AND_5_out, OR_9_out, NOT_13_out, MOV_5_out, SLL_4_out, SUB_5_out, ADDI_5_out, SUBI_5_out, MOVI_5_out);
  and and_6 (and_6_out, not_14_out, or_14_out);
  not not_14 (not_14_out, C4s);
  or or_14 (or_14_out, Sub, Subi);
  Multiplexer #(.select(4), .width(4)) multiplexer_1 (
    .in0(B), .in1(B), .in2(B), .in3(B), .in4(B), .in5(B), .in6(B), .in7(B), .in8(D), .in9(D), .in10(D),
    .in11(B), .in12(B), .in13(B), .in14(B), .in15(B), .out({B3, B2, B1, B0}), .sel(S));  // open: en
  or or_15 (C4, and_6_out, and_7_out);
  and and_7 (and_7_out, or_16_out, C4_t);
  or or_16 (or_16_out, Add, Addi);
  not not_15 (not_15_out, Cin);
  not not_16 (not_16_out, B0);
  not not_17 (not_17_out, B1);
  not not_18 (not_18_out, B2);
  not not_19 (not_19_out, B3);
  Adder adder_5 (.A(A[0]), .B(not_16_out), .Cin(not_15_out), .P(P0s), .G(G0s), .S(SUB0));  // open: Cout
  Adder adder_6 (.A(A[1]), .B(not_17_out), .Cin(C1outs), .P(P1s), .G(G1s), .S(SUB1));  // open: Cout
  Adder adder_7 (.A(A[2]), .B(not_18_out), .Cin(C2outs), .P(P2s), .G(G2s), .S(SUB2));  // open: Cout
  // Adder adder_8: pin names not known; wires that end beside it: adder_8_p1, adder_8_p1, A[3], not_19_out, C3outs, P3s, G3s, SUB3
  not not_20 (not_20_out, Cin);
  and and_8 (and_8_out, Cin, P0);
  and and_9 (and_9_out, Cin, P1, P0);
  and and_10 (and_10_out, G0, P1);
  and and_11 (and_11_out, Cin, P0, P1, P2);
  and and_12 (and_12_out, P1, P2, G0);
  and and_13 (and_13_out, P2, G1);
  and and_14 (and_14_out, Cin, P3, P2, P1, P0);
  and and_15 (and_15_out, G0, P1, P2, P3);
  and and_16 (and_16_out, G1, P2, P3);
  and and_17 (and_17_out, G2, P3);
  and and_18 (and_18_out, not_20_out, P0s);
  and and_19 (and_19_out, not_20_out, P1s, P0s);
  and and_20 (and_20_out, G0s, P1s);
  and and_21 (and_21_out, not_20_out, P0s, P1s, P2s);
  and and_22 (and_22_out, P1s, P2s, G0s);
  and and_23 (and_23_out, P2s, G1s);
  and and_24 (and_24_out, not_20_out, P3s, P2s, P1s, P0s);
  and and_25 (and_25_out, G0s, P1s, P2s, P3s);
  and and_26 (and_26_out, G1s, P2s, P3s);
  and and_27 (and_27_out, G2s, P3s);
  or or_17 (C1out, and_8_out, G0);
  or or_18 (C2out, and_9_out, and_10_out, G1);
  or or_19 (C3out, and_11_out, and_12_out, and_13_out, G2);
  or or_20 (C4_t, and_14_out, and_15_out, and_16_out, and_17_out, G3);
  or or_21 (C1outs, and_18_out, G0s);
  or or_22 (C2outs, and_19_out, and_20_out, G1s);
  or or_23 (C3outs, and_21_out, and_22_out, and_23_out, G2s);
  or or_24 (C4s, and_24_out, and_25_out, and_26_out, and_27_out, G3s);

  // Other names for the same wires on the sheet: C4o = C4; C0 = out_7[0]; C1 = out_7[1]; C2 = out_7[2]; C3 = out_7[3]
endmodule

module Adder (
  input  A,
  input  B,
  input  Cin,
  output P,
  output S,
  output Cout,
  output G
);

  wire and_2_out;

  xor xor_1 (P, A, B);
  and and_1 (G, A, B);
  xor xor_2 (S, P, Cin);
  and and_2 (and_2_out, P, Cin);
  or or_1 (Cout, and_2_out, G);
endmodule

module Subtracter (
  input  A,
  input  B,
  input  Cin,
  input  in_4,
  output S,
  output Cout
);

  wire and_1_out, and_2_out, xor_1_out;

  xor xor_1 (xor_1_out, A, B);
  and and_1 (and_1_out, A, B);
  xor xor_2 (S, xor_1_out, Cin);
  and and_2 (and_2_out, xor_1_out, Cin);
  or or_1 (Cout, and_2_out, and_1_out);
endmodule
